# Fritzing sketch PipeClimbingRobot (saved by Fritzing 0.9.3b)

parts:
  M1 = RioRand LM2596
  Raspberry_Pi_1 = Raspberry Pi 3 [part_number=RPI-3-V1.2]
  U1 = LIPO-1000mAh [package=lipo-1000]
  U2 = LIPO-1000mAh [package=lipo-1000]
  U3 = SWITCH_SPDT [package=kps-1290]
  M2 = L293D Motor Driver
  M3 = L293D Motor Driver
  M4 = DC Motor
  M5 = DC Motor
  M6 = DC Motor

nets:
  N1: M1.Pin_1, U3.O
  N2: M1.Pin_2, U1.-
  N3: M1.Pin_3, Raspberry_Pi_1.GPIO2, Raspberry_Pi_1.5V
  N4: M1.Pin_4, Raspberry_Pi_1.GND
  N5: Raspberry_Pi_1.GIPO13, Raspberry_Pi_1.GIPO19, M2.pin_6, M2.pin_7
  N6: Raspberry_Pi_1.GIPO26, M2.pin_5
  N7: Raspberry_Pi_1.GIPO21, M3.pin_8
  N8: Raspberry_Pi_1.GIPO20, M3.pin_7
  N9: Raspberry_Pi_1.ID_SC, M3.pin_6
  N10: Raspberry_Pi_1.GIPO7, M3.pin_5
  N11: U1.+, U2.-
  N12: U2.+, U3.P
  N13: M2.pin_9, M6.pin_1
  N14: M2.pin_10, M6.pin_2
  N15: M3.pin_9, M4.pin_1
  N16: M3.pin_10, M4.pin_2
  N17: M3.pin_11, M5.pin_1
  N18: M3.pin_12, M5.pin_2
